# Fritzing sketch shema electrique epareuse nunchuk (saved by Fritzing 0.9.3b)

parts:
  Composant1 = Arduino Nano (Rev3.0)
  Grove1 = Grove 3 Axis Digital Accelerometer 16g
  U1 = LM2596 step down module
  Composant2 = Arduino Motor Shield
  Composant3 = Arduino Motor Shield
  Composant4 = Arduino Motor Shield
  Composant5 = Arduino Motor Shield
  Composant6 = ACS712 Low Current Sensor Board v12
  Composant7 = ACS712 Low Current Sensor Board v12
  L2 = Solenoid
  L3 = Solenoid
  L4 = Solenoid
  L5 = Solenoid
  L6 = Solenoid
  L7 = Solenoid
  L8 = Solenoid
  L9 = Solenoid
  Composant8 = ACS712 Low Current Sensor Board v12

nets:
  GND: Composant1.GND, Grove1.GND, U1.IN-, U1.OUT-, Composant2.GND, Composant3.GND, Composant4.GND, Composant5.GND, Composant6.GND, Composant7.GND
  N1: Composant1.D2, Composant5.VIN
  N2: Composant1.D3, Composant5.RES
  N3: Composant1.D4, Composant4.VIN
  N4: Composant1.D5, Composant7.VO
  N5: Composant1.D6, Composant3.RX
  N6: Composant1.D7, Composant3.VIN
  N7: Composant1.D9, Composant4.RES
  N8: Composant1.D10, Composant2.RX
  N9: Composant1.D11/MOSI, Composant6.VO
  N10: Composant1.D12/MISO, Composant2.VIN
  5V: Composant1.VIN, U1.OUT+, Composant6.5V, Composant7.5V
  N11: Composant1.A5, Grove1.SCL
  N12: Composant1.A4, Grove1.SDA
  3V3: Composant1.3V3, Grove1.VCC
  N13: Composant1.D13/SCK, Composant8.VO
  N14: U1.IN+, L9.pin1
  N15: Composant2.OUT3, L2.pin2
  N16: Composant2.OUT4, L9.pin2
  N17: Composant3.OUT3, L4.pin2
  N18: Composant3.OUT4, L3.pin2
  N19: Composant4.OUT3, L5.pin2
  N20: Composant4.OUT4, L6.pin2
  N21: Composant5.OUT3, L7.pin2
  N22: Composant5.OUT4, L8.pin2

notes:
  branchement sur votre nunchuk
  arriver courant 12 v sur lm 2596 attention potentiometre a regler au multumetre avant branchement sur la nano en 5v sur vin
  les carte md10pot ressemble un peu a ces 4 cartes rouge de dessous a deux difference pres, je n'ai pas trouvé de carte plus ressemblante, il faudra adapté : sur la md10pot il n'y a pas de broche +5v elle est remplcé par une broche dir qui sert a definir la direction du moteur
  et une broche pwm sert a definir le voltage de sortie que je met sur la rst de la carte juste en remplacement de la pwm
  solenoide de commande haut bas
  solenoide de commande gauche droite
  solenoide de commande avncé reculé le bras
  solenoide de commande de pivot de la tete

custom parts:
  LM2596 step down module: LM2596 DC-DC step down power supply module 3 A.
